// Logisim project ARM_Single_Cycle.circ as structural Verilog
module main (
  input  CLR
);

  wire and_1_out, B, B_BL, B_BL_or_PC_out, BL, BX, clock_1_out, control_unit_1_alu_src,
       control_unit_1_memtoreg, control_unit_1_memwrite, control_unit_1_pcsrc, control_unit_1_regwrite, Mov,
       PC;
  wire [1:0] control_unit_1_alucontrol, control_unit_1_immsrc, control_unit_1_regsrc, wire_split_1_op;
  wire [3:0] alu2_1_nzcv, multiplexer_2_out, multiplexer_3_out, multiplexer_4_out, wire_split_1__3_0,
       wire_split_1__19_16, wire_split_1_cond, wire_split_1_rd_15_12;
  wire [5:0] wire_split_1_funct_20_25;
  wire [23:0] wire_split_1__23_0, wire_split_1_bx;
  wire [31:0] adder_1_out, adder_2_out, alu2_1_out_4, data_memory_out_6, Extend_result,
       Instruc_Mem_readdata_rd, multiplexer_1_out, multiplexer_5_out, multiplexer_6_out, multiplexer_7_out,
       multiplexer_8_out, multiplexer_9_out, multiplexer_10_out, multiplexer_11_out, PC_q,
       register_file_1_rd1, register_file_1_rd2, subtractor_1_out;

  Multiplexer #(.width(32), .disabled(0), .enable("false")) multiplexer_1 (
    .in0(adder_1_out), .in1(multiplexer_10_out), .out(multiplexer_1_out), .sel(control_unit_1_pcsrc));
  // Probe on multiplexer_1_out
  // Probe on adder_1_out
  // Probe on multiplexer_10_out
  // Probe on PC_q
  Register #(.width(32)) u_PC (.D(multiplexer_1_out), .Q(PC_q), .clk(clock_1_out), .clr(CLR));  // open: en
  // Probe on Instruc_Mem_readdata_rd
  instruction_memory Instruc_Mem (.in_1(PC_q), .ReadData_RD(Instruc_Mem_readdata_rd));
  Adder #(.width(32)) adder_1 (.a(PC_q), .b(32'h4), .out(adder_1_out));  // open: cin, cout
  Adder #(.width(32)) adder_2 (.a(32'h4), .b(adder_1_out), .out(adder_2_out));  // open: cin, cout
  Clock clock_1 (.out(clock_1_out));
  Wire_Split wire_split_1 (
    .From_Control(Instruc_Mem_readdata_rd), ._3_0(wire_split_1__3_0), .RD_15_12(wire_split_1_rd_15_12),
    ._19_16(wire_split_1__19_16), ._23_0(wire_split_1__23_0), .Cond(wire_split_1_cond), .Op(wire_split_1_op),
    .funct_20_25(wire_split_1_funct_20_25), .BX(wire_split_1_bx), .PC(PC));
  Multiplexer #(.width(4), .disabled(0), .enable("false")) multiplexer_2 (
    .in0(wire_split_1__19_16), .in1(4'b1111), .out(multiplexer_2_out), .sel(control_unit_1_regsrc[0]));
  Multiplexer #(.width(4), .disabled(0), .enable("false")) multiplexer_3 (
    .in0(wire_split_1_rd_15_12), .in1(4'b1110), .out(multiplexer_3_out), .sel(BL));
  Multiplexer #(.width(4), .disabled(0), .enable("false")) multiplexer_4 (
    .in0(wire_split_1__3_0), .in1(wire_split_1_rd_15_12), .out(multiplexer_4_out),
    .sel(control_unit_1_regsrc[1]));
  // Probe on multiplexer_3_out
  Multiplexer #(.width(32), .disabled(0), .enable("false")) multiplexer_5 (
    .in0(adder_2_out), .in1(PC_q), .out(multiplexer_5_out), .sel(and_1_out));
  and and_1 (and_1_out, PC, Mov);
  Multiplexer #(.width(32), .disabled(0), .enable("false")) multiplexer_6 (
    .in0(multiplexer_7_out), .in1(adder_2_out), .out(multiplexer_6_out), .sel(BL));
  control_unit control_unit_1 (
    .CLK(clock_1_out), .Cond_Flag(wire_split_1_cond), .ALU_Flags(alu2_1_nzcv), .Op(wire_split_1_op),
    .Funct(wire_split_1_funct_20_25), .Rd(wire_split_1_rd_15_12), .BX(wire_split_1_bx),
    .PCSrc(control_unit_1_pcsrc), .RegWrite(control_unit_1_regwrite), .MemWrite(control_unit_1_memwrite),
    .MemToReg(control_unit_1_memtoreg), .ALU_Src(control_unit_1_alu_src), .ImmSrc(control_unit_1_immsrc),
    .RegSrc(control_unit_1_regsrc), .ALUControl(control_unit_1_alucontrol), .Mov(Mov), .BX_2(BX), .BL(BL),
    .B(B));  // open: Mov_2
  // Probe on multiplexer_2_out
  // Probe on multiplexer_4_out
  // Probe on multiplexer_6_out
  Multiplexer #(.width(32), .disabled(0), .enable("false")) multiplexer_7 (
    .in0(multiplexer_10_out), .in1(multiplexer_8_out), .out(multiplexer_7_out), .sel(Mov));
  register_file register_file_1 (
    .Clock(clock_1_out), .Write_Enable_WE3(control_unit_1_regwrite), .Write_Port_A3(multiplexer_3_out),
    .Write_Data_WD3(multiplexer_6_out), .PC(multiplexer_5_out), .Clear(CLR), .RD1(register_file_1_rd1),
    .Read_Port_A1(multiplexer_2_out), .RD2(register_file_1_rd2), .Read_Port_A2(multiplexer_4_out));
  // Probe on multiplexer_5_out
  Extend Extend (.ImmSrc(control_unit_1_immsrc), ._23_0(wire_split_1__23_0), .RESULT(Extend_result));
  or or_1 (B_BL, BL, B);
  // Probe on register_file_1_rd1
  // Probe on register_file_1_rd2
  Multiplexer #(.width(32), .disabled(0), .enable("false")) multiplexer_8 (
    .in0(register_file_1_rd2), .in1(Extend_result), .out(multiplexer_8_out), .sel(control_unit_1_alu_src));
  // Probe on alu2_1_nzcv
  Multiplexer #(.width(32), .disabled(0), .enable("false")) multiplexer_9 (
    .in0(register_file_1_rd1), .in1({32{1'b0}}), .out(multiplexer_9_out), .sel(Mov));
  // Probe on control_unit_1_alucontrol
  // Probe on alu2_1_out_4
  ALU2 alu2_1 (
    .ALUControl(control_unit_1_alucontrol), .NZCV(alu2_1_nzcv), .out_4(alu2_1_out_4), .A(multiplexer_9_out),
    .B(multiplexer_8_out));
  // Probe on register_file_1_rd2
  // Probe on multiplexer_10_out
  // Probe on multiplexer_11_out
  // Probe on data_memory_out_6
  data_memory data_memory (
    .Clock(clock_1_out), .Address(alu2_1_out_4), .Write_Data_WD(register_file_1_rd2),
    .WE(control_unit_1_memwrite), .Clear(CLR), .out_6(data_memory_out_6));
  // Probe on alu2_1_out_4
  Multiplexer #(.width(32), .disabled(0), .enable("false")) multiplexer_10 (
    .in0(multiplexer_11_out), .in1(subtractor_1_out), .out(multiplexer_10_out), .sel(B_BL_or_PC_out));
  and B_BL_or_PC (B_BL_or_PC_out, ~B_BL, control_unit_1_pcsrc);  // AND_Gate
  Multiplexer #(.width(32), .disabled(0), .enable("false")) multiplexer_11 (
    .in0(alu2_1_out_4), .in1(data_memory_out_6), .out(multiplexer_11_out), .sel(control_unit_1_memtoreg));
  Subtractor #(.width(32)) subtractor_1 (.a(multiplexer_11_out), .b(32'h4), .out(subtractor_1_out));  // open: bin, bout
  // Probe on subtractor_1_out
endmodule

module register_file (
  input  Clock,
  input  Clear,
  input  Write_Enable_WE3,
  input  [3:0] Read_Port_A1,
  input  [3:0] Write_Port_A3,
  input  [3:0] Read_Port_A2,
  input  [31:0] Write_Data_WD3,
  input  [31:0] PC,
  output [31:0] RD1,
  output [31:0] RD2
);

  wire and_1_out, and_2_out, and_3_out, and_4_out, and_5_out, and_6_out, and_7_out, and_8_out, and_9_out,
       and_10_out, and_11_out, and_12_out, and_13_out, and_14_out, and_15_out, decoder_1_out0,
       decoder_1_out1, decoder_1_out2, decoder_1_out3, decoder_1_out4, decoder_1_out5, decoder_1_out6,
       decoder_1_out7, decoder_1_out8, decoder_1_out9, decoder_1_out10, decoder_1_out11, decoder_1_out12,
       decoder_1_out13, decoder_1_out14;
  wire [31:0] R0_q, R1_q, R2_q, R3_q, R4_q, R5_q, R6_q, R7_q, R8_q, R9_q, R10_q, R11_q, R12_q, R13_q, R14_q;

  Decoder #(.select(4)) decoder_1 (
    .out0(decoder_1_out0), .out1(decoder_1_out1), .out2(decoder_1_out2), .out3(decoder_1_out3),
    .out4(decoder_1_out4), .out5(decoder_1_out5), .out6(decoder_1_out6), .out7(decoder_1_out7),
    .out8(decoder_1_out8), .out9(decoder_1_out9), .out10(decoder_1_out10), .out11(decoder_1_out11),
    .out12(decoder_1_out12), .out13(decoder_1_out13), .out14(decoder_1_out14), .sel(Write_Port_A3));  // open: out15, en
  // Probe on Write_Port_A3
  and and_1 (and_1_out, Write_Enable_WE3, decoder_1_out0);
  and and_2 (and_2_out, Write_Enable_WE3, decoder_1_out1);
  and and_3 (and_3_out, Write_Enable_WE3, decoder_1_out2);
  and and_4 (and_4_out, Write_Enable_WE3, decoder_1_out3);
  and and_5 (and_5_out, Write_Enable_WE3, decoder_1_out4);
  and and_6 (and_6_out, Write_Enable_WE3, decoder_1_out5);
  and and_7 (and_7_out, Write_Enable_WE3, decoder_1_out6);
  and and_8 (and_8_out, Write_Enable_WE3, decoder_1_out7);
  and and_9 (and_9_out, Write_Enable_WE3, decoder_1_out8);
  and and_10 (and_10_out, Write_Enable_WE3, decoder_1_out9);
  and and_11 (and_11_out, Write_Enable_WE3, decoder_1_out10);
  and and_12 (and_12_out, Write_Enable_WE3, decoder_1_out11);
  and and_13 (and_13_out, Write_Enable_WE3, decoder_1_out12);
  and and_14 (and_14_out, Write_Enable_WE3, decoder_1_out13);
  and and_15 (and_15_out, Write_Enable_WE3, decoder_1_out14);
  Register #(.width(32)) R0 (.D(Write_Data_WD3), .en(and_1_out), .Q(R0_q), .clk(Clock), .clr(Clear));
  Register #(.width(32)) R1 (.D(Write_Data_WD3), .en(and_2_out), .Q(R1_q), .clk(Clock), .clr(Clear));
  Register #(.width(32)) R2 (.D(Write_Data_WD3), .en(and_3_out), .Q(R2_q), .clk(Clock), .clr(Clear));
  Register #(.width(32)) R3 (.D(Write_Data_WD3), .en(and_4_out), .Q(R3_q), .clk(Clock), .clr(Clear));
  Register #(.width(32)) R4 (.D(Write_Data_WD3), .en(and_5_out), .Q(R4_q), .clk(Clock), .clr(Clear));
  Register #(.width(32)) R5 (.D(Write_Data_WD3), .en(and_6_out), .Q(R5_q), .clk(Clock), .clr(Clear));
  Register #(.width(32)) R6 (.D(Write_Data_WD3), .en(and_7_out), .Q(R6_q), .clk(Clock), .clr(Clear));
  Register #(.width(32)) R7 (.D(Write_Data_WD3), .en(and_8_out), .Q(R7_q), .clk(Clock), .clr(Clear));
  Register #(.width(32)) R8 (.D(Write_Data_WD3), .en(and_9_out), .Q(R8_q), .clk(Clock), .clr(Clear));
  Register #(.width(32)) R9 (.D(Write_Data_WD3), .en(and_10_out), .Q(R9_q), .clk(Clock), .clr(Clear));
  Register #(.width(32)) R10 (.D(Write_Data_WD3), .en(and_11_out), .Q(R10_q), .clk(Clock), .clr(Clear));
  Register #(.width(32)) R11 (.D(Write_Data_WD3), .en(and_12_out), .Q(R11_q), .clk(Clock), .clr(Clear));
  Register #(.width(32)) R12 (.D(Write_Data_WD3), .en(and_13_out), .Q(R12_q), .clk(Clock), .clr(Clear));
  Register #(.width(32)) R13 (.D(Write_Data_WD3), .en(and_14_out), .Q(R13_q), .clk(Clock), .clr(Clear));
  Register #(.width(32)) R14 (.D(Write_Data_WD3), .en(and_15_out), .Q(R14_q), .clk(Clock), .clr(Clear));
  // Probe on R5_q
  // Probe on R4_q
  // Probe on R6_q
  // Probe on R7_q
  // Probe on R8_q
  // Probe on R9_q
  // Probe on R10_q
  // Probe on R11_q
  // Probe on R12_q
  // Probe on R13_q
  // Probe on R14_q
  // Probe on PC
  // Probe on R3_q
  // Probe on R2_q
  // Probe on R1_q
  // Probe on PC
  // Probe on R0_q
  Multiplexer #(.select(4), .width(32), .disabled(0), .enable("false")) multiplexer_1 (
    .in0(R0_q), .in1(R1_q), .in2(R2_q), .in3(R3_q), .in4(R4_q), .in5(R5_q), .in6(R6_q), .in7(R7_q),
    .in8(R8_q), .in9(R9_q), .in10(R10_q), .in11(R11_q), .in12(R12_q), .in13(R13_q), .in14(R14_q), .in15(PC),
    .out(RD2), .sel(Read_Port_A2));
  Multiplexer #(.select(4), .width(32), .disabled(0), .enable("false")) multiplexer_2 (
    .in0(R0_q), .in1(R1_q), .in2(R2_q), .in3(R3_q), .in4(R4_q), .in5(R5_q), .in6(R6_q), .in7(R7_q),
    .in8(R8_q), .in9(R9_q), .in10(R10_q), .in11(R11_q), .in12(R12_q), .in13(R13_q), .in14(R14_q), .in15(PC),
    .out(RD1), .sel(Read_Port_A1));
endmodule

module instruction_memory (
  input  [31:0] in_1,
  output [31:0] ReadData_RD
);

  ROM #(.dataWidth(32)) rom_1 (.addr(in_1[9:2]), .data(ReadData_RD), .sel(1'b1));
  // Probe on ReadData_RD

  // Notes on the sheet:
  //   contents of rom_1 (hex, n*v repeats v):
  //   e3a0d080 e08dd00d e08dd00d e08dd00d e3a00007 eb000000 eafffffe e3500000 a00000d e3500001 a00000b
  //   e3a02000 e3a01001 e3a03000 e3a04001 e1510000 a000004 e0832004 e1a03004 e1a04002 e2811001 eafffff8
  //   e1a00002 e12fff1e
endmodule

// data_mem
module data_memory (
  input  Clock,
  input  [31:0] Address,
  input  WE,
  input  Clear,
  input  [31:0] Write_Data_WD,
  output [31:0] out_6
);

  wire not_1_out;

  // Probe on Write_Data_WD
  RAM #(.dataWidth(32), .bus("separate")) ram_1 (
    .addr(Address[9:2]), .din(Write_Data_WD), .data(out_6), .str(WE), .sel(1'b1), .clk(Clock),
    .ld(not_1_out), .clr(Clear));
  not not_1 (not_1_out, WE);
  // Probe on out_6
endmodule

// Main
module main_decoder (
  input  [1:0] op,
  input  [5:0] funct,
  input  [23:0] BX,
  output Branch,
  output BL,
  output BX_2,
  output [1:0] ImmSrc,
  output MemToReg,
  output ALUSrc,
  output [1:0] Reg_Src,
  output MemW,
  output RegW,
  output ALU_Op,
  output MOV
);

  wire DP_Imm_out, DP_Reg_out, or_1_out, or_2_out, STR_out;

  Comparator #(.width(24)) comparator_1 (.a(BX), .b(24'h12fff1), .eq(BX_2));  // open: gt, lt
  and B (ImmSrc[1], op[1], ~op[0]);  // AND_Gate
  and u_BL (BL, op[1], ~op[0], funct[4]);  // AND_Gate
  and DP_Imm (DP_Imm_out, ~op[1], ~op[0], funct[5]);  // AND_Gate
  and DP_Reg (DP_Reg_out, ~op[1], ~op[0], ~funct[5]);  // AND_Gate
  buf or_1 (or_1_out, funct[0]);  // OR_Gate
  or or_2 (or_2_out, DP_Imm_out, DP_Reg_out);
  or or_3 (Branch, ImmSrc[1], BL);
  and LDR (MemToReg, ~op[1], op[0], or_1_out);  // AND_Gate
  and STR (STR_out, ~op[1], op[0], ~funct[0]);  // AND_Gate
  or or_4 (ALU_Op, DP_Imm_out, DP_Reg_out);
  and and_1 (MOV, or_2_out, funct[1], ~funct[2], funct[3], funct[4]);  // AND_Gate
  or or_5 (ALUSrc, ImmSrc[1], MemToReg, BX_2, STR_out, DP_Imm_out);
  or or_6 (RegW, MemToReg, DP_Imm_out, BL, DP_Reg_out);
  or or_7 (MemW, STR_out, BL);
  or or_8 (ImmSrc[0], MemToReg, STR_out);
  or or_9 (Reg_Src[1], MemToReg, STR_out);

  assign Reg_Src[0] = ImmSrc[1];
endmodule

module ALU (
  input  [31:0] A,
  input  [31:0] B,
  input  [1:0] ALU_Control,
  output [31:0] Result,
  output [3:0] NZCV
);

  wire adder_1_cout, not_1_out, xnor_1_out, xor_1_out;
  wire [31:0] adder_1_out, and_3_out, multiplexer_2_out, not_2_out, or_1_out;

  NotExactlyOne xnor_1 (.out(xnor_1_out), .in0(ALU_Control[0]), .in1(A[31]), .in2(B[31]));
  xor xor_1 (xor_1_out, A[31], adder_1_out[31]);
  and and_1 (NZCV[0], xnor_1_out, xor_1_out, not_1_out);
  not not_1 (not_1_out, ALU_Control[1]);
  and and_2 (NZCV[1], not_1_out, adder_1_cout);
  assign or_1_out = A | B;  // OR_Gate or_1, 32 bits wide
  Multiplexer #(.select(2), .width(32), .disabled(0), .enable("false")) multiplexer_1 (
    .in0(adder_1_out), .in1(adder_1_out), .in2(and_3_out), .in3(or_1_out), .out({NZCV[3], Result[30:0]}),
    .sel(ALU_Control));
  assign and_3_out = A & B;  // AND_Gate and_3, 32 bits wide
  // Probe on adder_1_out
  assign not_2_out = ~B;  // NOT_Gate not_2, 32 bits wide
  Multiplexer #(.width(32), .disabled(0), .enable("false")) multiplexer_2 (
    .in0(B), .in1(not_2_out), .out(multiplexer_2_out), .sel(ALU_Control[0]));
  Adder #(.width(32)) adder_1 (
    .a(multiplexer_2_out), .b(A), .out(adder_1_out), .cin(ALU_Control[0]), .cout(adder_1_cout));
  and and_4 (NZCV[2], ~NZCV[3], ~Result[30], ~Result[29], ~Result[28], ~Result[27], ~Result[26], ~Result[25], ~Result[24], ~Result[23], ~Result[22], ~Result[21], ~Result[20], ~Result[19], ~Result[18], ~Result[17], ~Result[16], ~Result[15], ~Result[14], ~Result[13], ~Result[12], ~Result[11], ~Result[10], ~Result[9], ~Result[8], ~Result[7], ~Result[6], ~Result[5], ~Result[4], ~Result[3], ~Result[2], ~Result[1], ~Result[0]);  // AND_Gate
  // Probe on multiplexer_2_out

  assign Result[31] = NZCV[3];
endmodule

module PC_Logic (
  input  [3:0] in_1,
  input  Reg_Write,
  input  Branch,
  output PCS
);

  wire and_1_out, comparator_1_eq;

  Comparator #(.width(4)) comparator_1 (.a(in_1), .b(4'b1111), .eq(comparator_1_eq));  // open: gt, lt
  and and_1 (and_1_out, comparator_1_eq, Reg_Write);
  or or_1 (PCS, and_1_out, Branch);
endmodule

module ALU_Decoder (
  input  [4:0] in_1,
  input  ALU_Op,
  output [1:0] ALU_Cntrl,
  output NoWrite,
  output [1:0] FlagW,
  output Mov
);

  wire Add_out, and_2_out, And_out, or_1_out, Orr_out, Sub_out;

  and Add (Add_out, ALU_Op, ~in_1[4], in_1[3], ~in_1[2], ~in_1[1]);  // AND_Gate
  and Sub (Sub_out, ALU_Op, ~in_1[4], ~in_1[3], in_1[2], ~in_1[1]);  // AND_Gate
  and CMP (NoWrite, ALU_Op, in_1[4], ~in_1[3], in_1[2], ~in_1[1], in_1[0]);  // AND_Gate
  and And (And_out, ALU_Op, ~in_1[4], ~in_1[3], ~in_1[2], ~in_1[1]);  // AND_Gate
  and Orr (Orr_out, ALU_Op, in_1[4], in_1[3], ~in_1[2], in_1[1]);  // AND_Gate
  and u_Mov (Mov, ALU_Op, in_1[4], in_1[3], ~in_1[2], in_1[1]);  // AND_Gate
  or or_1 (or_1_out, Add_out, Sub_out);
  or or_2 (ALU_Cntrl[1], And_out, Orr_out);
  and and_2 (and_2_out, or_1_out, in_1[0]);
  or or_3 (ALU_Cntrl[0], Sub_out, NoWrite, Orr_out);
  or or_4 (FlagW[0], and_2_out, NoWrite);

  assign FlagW[1] = in_1[0];
endmodule

module Extend (
  input  [1:0] ImmSrc,
  input  [23:0] _23_0,
  output [31:0] RESULT
);

  wire [23:0] demultiplexer_1_out0, demultiplexer_1_out1, demultiplexer_1_out2;
  wire [31:0] bit_extender_1_out, bit_extender_2_out;

  Demultiplexer #(.select(2), .width(24), .disabled(0), .enable("false")) demultiplexer_1 (
    .out0(demultiplexer_1_out0), .out1(demultiplexer_1_out1), .out2(demultiplexer_1_out2), .in(_23_0),
    .sel(ImmSrc));  // open: out3
  // Probe on {{7{demultiplexer_1_out2[23]}}, demultiplexer_1_out2[22:0], 2'b00}
  assign bit_extender_1_out = {{20{1'b0}}, demultiplexer_1_out1[11:0]};  // Bit_Extender bit_extender_1
  assign bit_extender_2_out = {{24{1'b0}}, demultiplexer_1_out0[7:0]};  // Bit_Extender bit_extender_2
  Multiplexer #(.select(2), .width(32)) multiplexer_1 (
    .in0(bit_extender_2_out), .in1(bit_extender_1_out),
    .in2({{7{demultiplexer_1_out2[23]}}, demultiplexer_1_out2[22:0], 2'b00}), .out(RESULT), .sel(ImmSrc));  // open: in3, en
  // Probe on bit_extender_1_out
  // Probe on bit_extender_2_out
endmodule

module Wire_Split (
  input  [31:0] From_Control,
  output [23:0] BX,
  output [3:0] _3_0,
  output PC,
  output [3:0] RD_15_12,
  output [3:0] _19_16,
  output [23:0] _23_0,
  output [3:0] Cond,
  output [1:0] Op,
  output [5:0] funct_20_25
);

  Comparator #(.width(4)) comparator_1 (.a(4'b1111), .b(From_Control[15:12]), .eq(PC));  // open: gt, lt

  assign _3_0 = From_Control[3:0];
  assign _19_16 = From_Control[19:16];
  assign _23_0 = From_Control[23:0];
  assign BX = From_Control[27:4];
  assign Cond = From_Control[31:28];
  assign funct_20_25 = From_Control[25:20];
  assign Op = From_Control[27:26];
  assign RD_15_12 = From_Control[15:12];
endmodule

// cond_ck
module condition_check (
  input  [3:0] Cond,
  input  [1:0] NZ,
  input  [1:0] CV,
  output CondEx
);

  wire AL_out, EQ_out, GE_out, GT_2_out, GT_out, LT_out, xnor_1_out;

  and GT (GT_out, Cond[3], Cond[2], ~Cond[1], ~Cond[0]);  // AND_Gate
  and EQ (EQ_out, ~Cond[3], ~Cond[2], ~Cond[1], ~Cond[0], NZ[0]);  // AND_Gate
  and GE (GE_out, Cond[3], ~Cond[2], Cond[1], ~Cond[0], ~NZ[1], ~CV[0]);  // AND_Gate
  and AL (AL_out, Cond[3], Cond[2], Cond[1], ~Cond[0]);  // AND_Gate
  xnor xnor_1 (xnor_1_out, NZ[0], CV[0]);
  and LT (LT_out, Cond[3], ~Cond[2], Cond[1], Cond[0], xnor_1_out);  // AND_Gate
  and GT_2 (GT_2_out, GT_out, xnor_1_out);
  or or_1 (CondEx, EQ_out, GE_out, AL_out, LT_out, GT_2_out);
endmodule

// ALU
module ALU2 (
  input  [31:0] A,
  input  [31:0] B,
  input  [1:0] ALUControl,
  output [31:0] out_4,
  output [3:0] NZCV
);

  wire adder_1_cout, not_1_out, xnor_1_out, xor_1_out;
  wire [31:0] adder_1_out, and_1_out, or_1_out, subtractor_1_out;

  // Probe on A
  Adder #(.width(32)) adder_1 (.a(B), .b(A), .out(adder_1_out), .cout(adder_1_cout));  // open: cin
  Subtractor #(.width(32)) subtractor_1 (.a(A), .b(B), .out(subtractor_1_out));  // open: bin, bout
  xor xor_1 (xor_1_out, adder_1_out[31], A[31]);
  NotExactlyOne xnor_1 (.out(xnor_1_out), .in0(ALUControl[0]), .in2(B[31]), .in4(A[31]));
  assign and_1_out = A & B;  // AND_Gate and_1, 32 bits wide
  assign or_1_out = A | B;  // OR_Gate or_1, 32 bits wide
  not not_1 (not_1_out, ALUControl[1]);
  Multiplexer #(.select(2), .width(32), .disabled(0), .enable("false")) multiplexer_1 (
    .in0(adder_1_out), .in1(subtractor_1_out), .in2(and_1_out), .in3(or_1_out), .out({NZCV[3], out_4[30:0]}),
    .sel(ALUControl));
  and and_2 (NZCV[1], adder_1_cout, not_1_out);
  and and_3 (NZCV[0], not_1_out, xor_1_out, xnor_1_out);
  and and_4 (NZCV[2], ~NZCV[3], ~out_4[30], ~out_4[29], ~out_4[28], ~out_4[27], ~out_4[26], ~out_4[25], ~out_4[24], ~out_4[23], ~out_4[22], ~out_4[21], ~out_4[20], ~out_4[19], ~out_4[18], ~out_4[17], ~out_4[16], ~out_4[15], ~out_4[14], ~out_4[13], ~out_4[12], ~out_4[11], ~out_4[10], ~out_4[9], ~out_4[8], ~out_4[7], ~out_4[6], ~out_4[5], ~out_4[4], ~out_4[3], ~out_4[2], ~out_4[1], ~out_4[0]);  // AND_Gate

  assign out_4[31] = NZCV[3];
endmodule

module tunnel (
  input  in_1,
  output out_2
);


  assign out_2 = in_1;

  // Other names for the same wires on the sheet: A = in_1
endmodule

// Decoder
module decoder (
  input  [3:0] Rd,
  input  [23:0] BX,
  input  [1:0] Op,
  input  [5:0] Funct,
  output PCS,
  output B,
  output BL,
  output BX_2,
  output Mov,
  output RegW,
  output MemW,
  output MemToReg,
  output ALUSrc,
  output [1:0] ImmSrc,
  output [1:0] RegSrc,
  output NoWrite,
  output [1:0] ALUControl,
  output [1:0] FlagW,
  output Mov_2
);

  wire main_decoder_1_alu_op;

  main_decoder main_decoder_1 (
    .op(Op), .funct(Funct), .Branch(B), .ALU_Op(main_decoder_1_alu_op), .Reg_Src(RegSrc), .RegW(RegW),
    .ImmSrc(ImmSrc), .ALUSrc(ALUSrc), .MemW(MemW), .BX(BX), .MemToReg(MemToReg), .MOV(Mov), .BL(BL),
    .BX_2(BX_2));
  ALU_Decoder alu_decoder_1 (
    .in_1(Funct[4:0]), .NoWrite(NoWrite), .FlagW(FlagW), .Mov(Mov_2), .ALU_Op(main_decoder_1_alu_op),
    .ALU_Cntrl(ALUControl));
  PC_Logic pc_logic_1 (.in_1(Rd), .Reg_Write(RegW), .Branch(B), .PCS(PCS));
endmodule

// Condition_Logic
module condition_logic (
  input  PCSrc,
  input  RegW,
  input  NoWrite,
  input  MemWrite,
  input  [1:0] FlagW,
  input  [3:0] Cond,
  input  [3:0] ALUFlags,
  input  CLK,
  output PCSrc_2,
  output RegWrite,
  output MemWrite_2
);

  wire condition_check_1_condex;
  wire [1:0] and_1_out, bit_extender_1_out, register_1_q, register_2_q;

  assign and_1_out = FlagW & bit_extender_1_out;  // AND_Gate and_1, 2 bits wide
  Register #(.width(2)) register_1 (.D(ALUFlags[3:2]), .Q(register_1_q), .clk(CLK), .clr(and_1_out[1]));  // open: en
  Register #(.width(2)) register_2 (.D(ALUFlags[1:0]), .Q(register_2_q), .clk(CLK), .clr(and_1_out[0]));  // open: en
  condition_check condition_check_1 (
    .Cond(Cond), .NZ(register_1_q), .CV(register_2_q), .CondEx(condition_check_1_condex));
  and and_2 (PCSrc_2, PCSrc, condition_check_1_condex);
  and and_3 (RegWrite, RegW, ~NoWrite, condition_check_1_condex);  // AND_Gate
  and and_4 (MemWrite_2, MemWrite, condition_check_1_condex);
  assign bit_extender_1_out = {{1{1'b0}}, condition_check_1_condex};  // Bit_Extender bit_extender_1
endmodule

module control_unit (
  input  CLK,
  input  [3:0] Cond_Flag,
  input  [3:0] ALU_Flags,
  input  [1:0] Op,
  input  [5:0] Funct,
  input  [3:0] Rd,
  input  [23:0] BX,
  output PCSrc,
  output RegWrite,
  output MemWrite,
  output MemToReg,
  output ALU_Src,
  output [1:0] ImmSrc,
  output [1:0] RegSrc,
  output [1:0] ALUControl,
  output Mov,
  output BX_2,
  output BL,
  output B,
  output Mov_2
);

  wire decoder_1_memw, decoder_1_nowrite, decoder_1_pcs, decoder_1_regw;
  wire [1:0] decoder_1_flagw;

  decoder decoder_1 (
    .Rd(Rd), .BX(BX), .Op(Op), .Funct(Funct), .PCS(decoder_1_pcs), .BX_2(BX_2), .BL(BL), .B(B), .Mov(Mov_2),
    .RegW(decoder_1_regw), .MemW(decoder_1_memw), .MemToReg(MemToReg), .ALUSrc(ALU_Src), .ImmSrc(ImmSrc),
    .RegSrc(RegSrc), .NoWrite(decoder_1_nowrite), .ALUControl(ALUControl), .FlagW(decoder_1_flagw),
    .Mov_2(Mov));
  condition_logic condition_logic_1 (
    .PCSrc(decoder_1_pcs), .RegW(decoder_1_regw), .NoWrite(decoder_1_nowrite), .MemWrite(decoder_1_memw),
    .FlagW(decoder_1_flagw), .Cond(Cond_Flag), .ALUFlags(ALU_Flags), .CLK(CLK), .PCSrc_2(PCSrc),
    .RegWrite(RegWrite), .MemWrite_2(MemWrite));
endmodule
